# Fritzing sketch tcan455x-bob-fritzing (saved by Fritzing 0.9.6b)
breadboards: 2

parts:
  Part1 = TCAN4551-BoB-R2B
  Part2 = nRF52 DK
  BAT1 = BC9VPC [package=bc9vpc]
  Part3 = TCAN4551-BoB-R2B

nets:
  N1: Part1.CAN_IF_SCLK, Part2.30
  N2: Part1.CAN_IF_MOSI, Part2.29
  N3: Part1.CAN_IF_MISO, Part2.28
  N4: Part1.CAN_IF_!CS, Part2.4
  N5: Part1.CAN_!INT, Part2.3
  GND: Part1.GND, Part2.GND, BAT1.V+, Part3.GND
  N6: Part1.12V_IN, BAT1.V-, Part3.12V_IN
  N7: Part1.VDD_IO, Part2.VDD#255
  N8: Part1.CAN_RST, Part2.31
  N9: Part2.27, Part3.CAN_IF_SCLK
  N10: Part2.26, Part3.CAN_IF_MOSI
  N11: Part2.2, Part3.CAN_IF_MISO
  N12: Part2.25, Part3.CAN_IF_!CS
  N13: Part2.24, Part3.CAN_!INT
  N14: Part2.23, Part3.CAN_RST
  N15: Part2.VDD#254, Part3.VDD_IO

custom parts:
  nRF52 DK: The nRF52 DK is a versatile single board development kit for Bluetooth® Smart, ANT and 2.4GHz proprietary applications using the nRF52832 SoC. This kit supports development for the nRF52832 SoC. The kit is hardware compatible with the Arduino Uno Revision 3 standard, making it possible to use 3rd-party shields that are compatible to this standard. An NFC antenna can be connected the kit to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
